# Fritzing sketch scheme (saved by Fritzing 0.9.3b)
breadboards: 1

parts:
  Onderdeel1 = Arduino Leonardo (Rev3b)
  R1 = Resistor [tolerance=±5% resistance=1M package=THT]
  R2 = Resistor [tolerance=±5% resistance=1M package=THT]
  R3 = Resistor [tolerance=±5% resistance=1M package=THT]
  R4 = Resistor [tolerance=±5% resistance=1M package=THT]
  R5 = Resistor [tolerance=±5% resistance=1M package=THT]
  R6 = Resistor [tolerance=±5% resistance=1M package=THT]
  J1 = Piezo Speaker
  J2 = Piezo Speaker
  J3 = Piezo Speaker
  J4 = Piezo Speaker
  J5 = Piezo Speaker
  J6 = Piezo Speaker

nets:
  N1: Onderdeel1.GND, R1.Pin_0, R2.Pin_0, R3.Pin_0, R4.Pin_0, R5.Pin_0, R6.Pin_0, J1.pin1, J2.pin1, J3.pin1, J4.pin1, J5.pin1, J6.pin1
  N2: Onderdeel1.A0, R6.Pin_1, J6.pin2
  N3: Onderdeel1.A1, R5.Pin_1, J5.pin2
  N4: Onderdeel1.A2, R1.Pin_1, J4.pin2
  N5: Onderdeel1.A3, R4.Pin_1, J2.pin2
  N6: Onderdeel1.A4, R3.Pin_1, J3.pin2
  N7: Onderdeel1.A5, R2.Pin_1, J1.pin2
